// Logisim project 4-Bit Adder & Subtractor.circ as structural Verilog: 2 circuits, main circuit Full Adder
module Full_Adder (
  input  A,
  input  B,
  input  C_IN,
  input  A_2,
  input  B_2,
  input  C_IN_2,
  output SUM,
  output C_Out,
  output SUM_2,
  output C_Out_2
);

  wire and_1_out, and_2_out, and_3_out, and_4_out, xor_1_out, xor_2_out;

  xor xor_1 (xor_1_out, A, B);
  and and_1 (and_1_out, A, B);
  xor xor_2 (xor_2_out, A_2, B_2);
  and and_2 (and_2_out, A_2, B_2);
  and and_3 (and_3_out, xor_1_out, C_IN);
  xor xor_3 (SUM, xor_1_out, C_IN);
  and and_4 (and_4_out, xor_2_out, C_IN_2);
  or or_1 (C_Out, and_1_out, and_3_out);
  xor xor_4 (SUM_2, xor_2_out, C_IN_2);
  or or_2 (C_Out_2, and_2_out, and_4_out);

  // Notes on the sheet:
  //   FULL ADDER
  //   FULL ADDER
endmodule

module _4_bit_adder (
  input  B0,
  input  A0,
  input  B1,
  input  A1,
  input  B2,
  input  A2,
  input  B3,
  input  A3,
  input  CARRY_BIT,
  output C_OUT,
  output S0,
  output S1,
  output S2,
  output S3
);

  wire full_adder_1_c_out, full_adder_2_c_out, full_adder_3_c_out;

  Full_Adder full_adder_1 (
    .B(A0), .C_IN(B0), .A_2(CARRY_BIT), .SUM(S0), .C_Out(full_adder_1_c_out));  // open: A, B_2, C_IN_2, SUM_2, C_Out_2
  Full_Adder full_adder_2 (
    .B(A1), .C_IN(B1), .A_2(full_adder_1_c_out), .SUM(S1), .C_Out(full_adder_2_c_out));  // open: A, B_2, C_IN_2, SUM_2, C_Out_2
  Full_Adder full_adder_3 (
    .B(A2), .C_IN(B2), .A_2(full_adder_2_c_out), .SUM(S2), .C_Out(full_adder_3_c_out));  // open: A, B_2, C_IN_2, SUM_2, C_Out_2
  Full_Adder full_adder_4 (
    .B(A3), .C_IN(B3), .A_2(full_adder_3_c_out), .SUM(S3), .C_Out(C_OUT));  // open: A, B_2, C_IN_2, SUM_2, C_Out_2

  // Notes on the sheet:
  //   4 BIT ADDER
endmodule
