// Logisim project Encoder_&_Decoder.circ as structural Verilog: 1 circuit, main circuit main
module main (
  input  A,
  input  B,
  input  C,
  input  D,
  input  A_2,
  input  B_2,
  output OUTPUT_1,
  output OUTPUT_2,
  output OUTPUT_1_2,
  output OUTPUT_2_2,
  output OUTPUT_3,
  output OUTPUT_4
);

  wire not_1_out, not_2_out;

  not not_1 (not_1_out, A_2);
  not not_2 (not_2_out, B_2);
  or or_1 (OUTPUT_1, C, D, A);
  or or_2 (OUTPUT_2, D, B, A);
  and and_1 (OUTPUT_1_2, not_1_out, not_2_out);
  and and_2 (OUTPUT_2_2, A_2, not_2_out);
  and and_3 (OUTPUT_3, not_1_out, B_2);
  and and_4 (OUTPUT_4, B_2, A_2);

  // Notes on the sheet:
  //   ENCODER
  //   DECODER
endmodule
