// Logisim project Multiplexer & Demultiplexer.circ as structural Verilog: 1 circuit, main circuit main
module main (
  input  A,
  input  B,
  input  Fixed_input_D,
  input  A_2,
  input  SUM,
  input  B_2
);

  wire and_1_out, and_2_out, and_3_out, and_4_out, and_5_out, and_6_out, not_1_out, not_2_out, not_3_out,
       or_1_out;

  not not_1 (not_1_out, SUM);
  and and_1 (and_1_out, A_2, SUM);
  and and_2 (and_2_out, B_2, not_1_out);
  or or_1 (or_1_out, and_1_out, and_2_out);
  LED led_1 (.in(or_1_out));
  not not_2 (not_2_out, A);
  not not_3 (not_3_out, B);
  and and_3 (and_3_out, Fixed_input_D, not_3_out, not_2_out);
  and and_4 (and_4_out, Fixed_input_D, not_3_out, A);
  and and_5 (and_5_out, Fixed_input_D, B, not_2_out);
  and and_6 (and_6_out, Fixed_input_D, B, A);
  LED led_2 (.in(and_3_out));
  LED led_3 (.in(and_4_out));
  LED led_4 (.in(and_5_out));
  LED led_5 (.in(and_6_out));

  // Notes on the sheet:
  //   Multiplexer
  //   Demultiplexer
endmodule
