// Logisim project 4-bit Register & 3-bit Counter.circ as structural Verilog: 1 circuit, main circuit main
module main (
  input  in_1,
  input  in_2,
  input  in_3,
  output out_4,
  output out_5,
  output out_6
);

  wire clock_1_out, d_ff_1_q, d_ff_1_qn, d_ff_2_q, d_ff_2_qn, d_ff_3_q, d_ff_3_qn, d_ff_4_q, j_k_ff_1_q,
       j_k_ff_2_q;

  Clock clock_1 (.out(clock_1_out));
  D_Flip_Flop d_ff_1 (.clk(in_2), .D(in_1), .Q(d_ff_1_q), .Qn(d_ff_1_qn));  // open: preset, en, reset
  J_K_Flip_Flop j_k_ff_1 (
    .J(in_3), .clk(clock_1_out), .K(in_3), .Q(j_k_ff_1_q), .Qn(out_6));  // open: preset, en, reset
  LED led_1 (.in(d_ff_1_q));
  LED led_2 (.in(d_ff_2_q));
  D_Flip_Flop d_ff_2 (.clk(in_2), .D(d_ff_1_qn), .Q(d_ff_2_q), .Qn(d_ff_2_qn));  // open: preset, en, reset
  J_K_Flip_Flop j_k_ff_2 (.J(in_3), .clk(j_k_ff_1_q), .K(in_3), .Q(j_k_ff_2_q), .Qn(out_5));  // open: preset, en, reset
  D_Flip_Flop d_ff_3 (.clk(in_2), .D(d_ff_2_qn), .Q(d_ff_3_q), .Qn(d_ff_3_qn));  // open: preset, en, reset
  LED led_3 (.in(d_ff_3_q));
  J_K_Flip_Flop j_k_ff_3 (.J(in_3), .clk(j_k_ff_2_q), .K(in_3), .Qn(out_4));  // open: Q, preset, en, reset
  LED led_4 (.in(d_ff_4_q));
  D_Flip_Flop d_ff_4 (.clk(in_2), .D(d_ff_3_qn), .Q(d_ff_4_q));  // open: Qn, preset, en, reset

  // Notes on the sheet:
  //   4-bit Register using D flip flop
  //   3-bit Binary Up Counter using JK flip flop
endmodule
